// Logisim project q1.circ as structural Verilog: 16 circuits, main circuit AND gate
module AND_gate (
  input  A,
  input  A_2,
  input  B,
  input  B_2,
  input  A_3,
  input  A_4,
  input  A_5,
  input  B_3,
  input  B_4,
  input  A_6,
  input  A_7,
  input  B_5,
  input  B_6,
  output O,
  output O_2,
  output O_3,
  output O_4,
  output O_5,
  output O_6,
  output O_7
);

  and and_1 (O, A, B);
  not not_1 (O_3, A_3);
  nand nand_1 (O_4, A_4, B_3);
  xor xor_1 (O_6, A_6, B_5);
  or or_1 (O_2, A_2, B_2);
  nor nor_1 (O_5, A_5, B_4);
  xnor xnor_1 (O_7, A_7, B_6);

  // Notes on the sheet:
  //   AND Gate
  //   NOT Gate
  //   NAND Gate
  //   XOR Gate
  //   OR Gate
  //   NOR Gate
  //   XNOR Gate
endmodule

module q2 (
  input  A,
  input  A_2,
  input  B,
  input  B_2,
  output O
);


  // Notes on the sheet:
  //   USING NAND GATES
endmodule

module \or  (
  input  A,
  input  B,
  output O
);

  wire nand_1_out, nand_2_out;

  nand nand_1 (nand_1_out, A, A);
  nand nand_2 (nand_2_out, B, B);
  nand nand_3 (O, nand_1_out, nand_2_out);
endmodule

module \not  (
  input  A,
  input  B,
  output O
);

  nand nand_1 (O, A, A);
endmodule

module \nor  (
  input  A,
  input  B,
  output O
);

  wire nand_1_out, nand_2_out, nand_3_out;

  nand nand_1 (nand_1_out, A, A);
  nand nand_2 (nand_2_out, B, B);
  nand nand_3 (nand_3_out, nand_1_out, nand_2_out);
  nand nand_4 (O, nand_3_out, nand_3_out);
endmodule

module \xor  (
  input  A,
  input  B,
  output O
);

  wire nand_1_out, nand_2_out, nand_3_out, nand_4_out;

  nand nand_1 (nand_1_out, B, B);
  nand nand_2 (nand_2_out, A, A);
  nand nand_3 (nand_3_out, A, nand_1_out);
  nand nand_4 (nand_4_out, B, nand_2_out);
  nand nand_5 (O, nand_3_out, nand_4_out);
endmodule

module XNOR (
  input  A,
  input  B,
  output O
);

  wire nand_1_out, nand_2_out, nand_3_out, nand_4_out;

  nand nand_1 (nand_1_out, A, A);
  nand nand_2 (nand_2_out, B, B);
  nand nand_3 (nand_3_out, nand_1_out, nand_2_out);
  nand nand_4 (nand_4_out, A, B);
  nand nand_5 (O, nand_3_out, nand_4_out);
endmodule

module _9com (
  input  A,
  input  B,
  input  C,
  input  D,
  output W,
  output X,
  output Y,
  output Z
);

  wire nand_1_out, nand_2_out, nand_3_out, nand_4_out, nand_5_out, nand_7_out, nand_8_out, nand_9_out;

  nand nand_1 (nand_1_out, A, A);
  nand nand_2 (nand_2_out, B, B);
  nand nand_3 (nand_3_out, C, C);
  nand nand_4 (nand_4_out, B, B);
  nand nand_5 (nand_5_out, C, C);
  nand nand_6 (Z, D, D);
  nand nand_7 (nand_7_out, nand_1_out, nand_2_out, nand_3_out);
  nand nand_8 (nand_8_out, nand_4_out, C);
  nand nand_9 (nand_9_out, B, nand_5_out);
  nand nand_10 (W, nand_7_out, nand_7_out);
  nand nand_11 (X, nand_8_out, nand_9_out);

  assign Y = C;
endmodule

module _10_scomp (
  input  A,
  input  B,
  input  C,
  input  D,
  output W,
  output X,
  output Y,
  output Z
);

  wire nand_1_out, nand_2_out, nand_3_out, nand_4_out, nand_5_out, nand_6_out, nand_7_out, nand_8_out,
       nand_9_out, nand_10_out, nand_11_out, nand_12_out, nand_13_out, nand_14_out, nand_15_out, nand_16_out,
       nand_17_out, nand_18_out, nand_19_out, nand_20_out, nand_21_out, nand_22_out, nand_23_out;

  nand nand_1 (nand_1_out, A, A);
  nand nand_2 (nand_2_out, B, B);
  nand nand_3 (nand_3_out, C, C);
  nand nand_4 (nand_4_out, A, A);
  nand nand_5 (nand_5_out, B, B);
  nand nand_6 (nand_6_out, D, D);
  nand nand_7 (nand_7_out, B, B);
  nand nand_8 (nand_8_out, C, C);
  nand nand_9 (nand_9_out, D, D);
  nand nand_10 (nand_10_out, C, C);
  nand nand_11 (nand_11_out, D, D);
  nand nand_12 (nand_12_out, A, A);
  nand nand_13 (nand_13_out, B, B);
  nand nand_14 (nand_14_out, C, C);
  nand nand_15 (nand_15_out, nand_1_out, nand_2_out, nand_3_out);
  nand nand_16 (nand_16_out, nand_4_out, nand_5_out, nand_6_out);
  nand nand_17 (nand_17_out, nand_7_out, C, D);
  nand nand_18 (nand_18_out, B, nand_8_out);
  nand nand_19 (nand_19_out, B, nand_9_out);
  nand nand_20 (nand_20_out, nand_10_out, nand_11_out);
  nand nand_21 (nand_21_out, C, D);
  nand nand_22 (nand_22_out, nand_12_out, nand_13_out, nand_14_out);
  nand nand_23 (nand_23_out, D, D);
  nand nand_24 (W, nand_15_out, nand_16_out);
  nand nand_25 (X, nand_17_out, nand_18_out, nand_19_out);
  nand nand_26 (Y, nand_20_out, nand_21_out);
  nand nand_27 (Z, nand_22_out, nand_23_out);
endmodule

module Binary_to__Gray_code (
  input  A,
  input  B,
  input  C,
  input  D,
  output W,
  output X,
  output Y,
  output Z
);

  wire and_1_out, and_2_out, and_3_out, and_4_out, and_5_out, and_6_out, not_1_out, not_2_out, not_3_out,
       not_4_out, not_5_out, not_6_out;

  not not_1 (not_1_out, A);
  and and_1 (and_1_out, not_1_out, B);
  and and_2 (and_2_out, A, not_2_out);
  not not_2 (not_2_out, B);
  not not_3 (not_3_out, B);
  and and_3 (and_3_out, not_3_out, C);
  and and_4 (and_4_out, B, not_4_out);
  not not_4 (not_4_out, C);
  not not_5 (not_5_out, C);
  and and_5 (and_5_out, not_5_out, D);
  and and_6 (and_6_out, C, not_6_out);
  not not_6 (not_6_out, D);
  or or_1 (X, and_1_out, and_2_out);
  or or_2 (Y, and_3_out, and_4_out);
  or or_3 (Z, and_5_out, and_6_out);

  assign W = A;
endmodule

module Gray_to_Binary (
  input  A,
  input  B,
  input  C,
  input  D,
  output W,
  output X,
  output Y,
  output Z
);

  wire and_1_out, and_2_out, and_3_out, and_4_out, and_5_out, and_6_out, and_7_out, and_8_out, and_9_out,
       and_10_out, and_11_out, and_12_out, and_13_out, and_14_out, not_1_out, not_2_out, not_3_out,
       not_4_out, not_5_out, not_6_out, not_7_out, not_8_out, not_9_out, not_10_out, not_11_out, not_12_out,
       not_13_out, not_14_out, not_15_out, not_16_out, not_17_out, not_18_out, not_19_out, not_20_out,
       not_21_out, not_22_out, not_23_out, not_24_out;

  not not_1 (not_1_out, A);
  and and_1 (and_1_out, not_1_out, B);
  and and_2 (and_2_out, A, not_2_out);
  not not_2 (not_2_out, B);
  not not_3 (not_3_out, A);
  not not_4 (not_4_out, B);
  and and_3 (and_3_out, not_3_out, not_4_out, C);
  not not_5 (not_5_out, A);
  and and_4 (and_4_out, not_5_out, B, not_6_out);
  not not_6 (not_6_out, C);
  and and_5 (and_5_out, A, not_7_out, not_8_out);
  not not_7 (not_7_out, B);
  not not_8 (not_8_out, C);
  and and_6 (and_6_out, A, B, C);
  not not_9 (not_9_out, A);
  not not_10 (not_10_out, B);
  not not_11 (not_11_out, C);
  not not_12 (not_12_out, A);
  not not_13 (not_13_out, B);
  not not_14 (not_14_out, D);
  not not_15 (not_15_out, A);
  not not_16 (not_16_out, C);
  not not_17 (not_17_out, D);
  not not_18 (not_18_out, A);
  not not_19 (not_19_out, B);
  not not_20 (not_20_out, C);
  not not_21 (not_21_out, D);
  not not_22 (not_22_out, B);
  not not_23 (not_23_out, C);
  not not_24 (not_24_out, D);
  or or_1 (X, and_1_out, and_2_out);
  or or_2 (Y, and_3_out, and_4_out, and_5_out, and_6_out);
  and and_7 (and_7_out, not_9_out, not_10_out, not_11_out, D);
  and and_8 (and_8_out, not_12_out, not_13_out, C, not_14_out);
  and and_9 (and_9_out, not_15_out, B, not_16_out, not_17_out);
  and and_10 (and_10_out, not_18_out, B, C, D);
  and and_11 (and_11_out, A, not_19_out, not_20_out, not_21_out);
  and and_12 (and_12_out, A, not_22_out, C, D);
  and and_13 (and_13_out, A, B, not_23_out, D);
  and and_14 (and_14_out, A, B, C, not_24_out);
  or or_3 (Z, and_7_out, and_8_out, and_9_out, and_10_out, and_11_out, and_12_out, and_13_out, and_14_out);

  assign W = A;
endmodule

module BCD_to_excess_3 (
  input  A,
  input  B,
  input  C,
  input  D,
  output W,
  output X,
  output Y,
  output Z
);

  wire and_1_out, and_2_out, and_3_out, and_4_out, and_5_out, and_6_out, and_7_out, not_1_out, not_2_out,
       not_3_out, not_4_out, not_5_out, not_6_out;

  and and_1 (and_1_out, B, D);
  and and_2 (and_2_out, B, C);
  not not_1 (not_1_out, B);
  and and_3 (and_3_out, not_1_out, D);
  not not_2 (not_2_out, B);
  and and_4 (and_4_out, not_2_out, C);
  and and_5 (and_5_out, B, not_3_out, not_4_out);
  not not_3 (not_3_out, C);
  not not_4 (not_4_out, D);
  not not_5 (not_5_out, C);
  and and_6 (and_6_out, not_5_out, not_6_out);
  not not_6 (not_6_out, D);
  and and_7 (and_7_out, C, D);
  not not_7 (Z, D);
  or or_1 (W, and_1_out, and_2_out, A);
  or or_2 (X, and_3_out, and_4_out, and_5_out);
  or or_3 (Y, and_6_out, and_7_out);
endmodule

module Excess_3_to_BCD (
  input  A,
  input  B,
  input  C,
  input  D,
  output W,
  output X,
  output Y,
  output Z
);

  wire and_1_out, and_2_out, and_3_out, and_4_out, and_5_out, and_6_out, and_7_out, not_1_out, not_2_out,
       not_3_out, not_4_out, not_5_out, not_6_out;

  and and_1 (and_1_out, A, C, D);
  and and_2 (and_2_out, A, B);
  not not_1 (not_1_out, B);
  and and_3 (and_3_out, not_1_out, not_2_out);
  not not_2 (not_2_out, C);
  not not_3 (not_3_out, B);
  and and_4 (and_4_out, not_3_out, not_4_out);
  not not_4 (not_4_out, D);
  and and_5 (and_5_out, B, C, D);
  not not_5 (not_5_out, C);
  and and_6 (and_6_out, not_5_out, D);
  and and_7 (and_7_out, C, not_6_out);
  not not_6 (not_6_out, D);
  not not_7 (Z, D);
  or or_1 (W, and_1_out, and_2_out);
  or or_2 (X, and_3_out, and_4_out, and_5_out);
  or or_3 (Y, and_6_out, and_7_out);
endmodule

module Square (
  input  A,
  input  B,
  input  C,
  input  D,
  output Q,
  output W,
  output E,
  output R,
  output T,
  output Y,
  output U,
  output I
);

  wire and_2_out, and_3_out, and_4_out, and_5_out, and_6_out, and_7_out, and_8_out, and_9_out, and_11_out,
       and_12_out, and_13_out, and_14_out, and_15_out, and_16_out, and_17_out, and_18_out, and_19_out,
       and_20_out, not_1_out, not_2_out, not_3_out, not_4_out, not_5_out, not_6_out, not_7_out, not_8_out,
       not_9_out, not_10_out, or_2_out, or_3_out;

  and and_1 (Q, A, B);
  and and_2 (and_2_out, A, not_1_out);
  not not_1 (not_1_out, B);
  and and_3 (and_3_out, A, C);
  not not_2 (not_2_out, A);
  and and_4 (and_4_out, not_2_out, B);
  and and_5 (and_5_out, A, not_3_out);
  not not_3 (not_3_out, B);
  and and_6 (and_6_out, B, not_4_out);
  not not_4 (not_4_out, C);
  not not_5 (not_5_out, D);
  not not_6 (not_6_out, A);
  and and_7 (and_7_out, not_6_out, B);
  not not_7 (not_7_out, B);
  not not_8 (not_8_out, B);
  and and_8 (and_8_out, not_8_out, C);
  and and_9 (and_9_out, B, not_9_out);
  not not_9 (not_9_out, C);
  and and_10 (Y, C, not_10_out);
  not not_10 (not_10_out, D);
  or or_1 (W, and_2_out, and_3_out);
  and and_11 (and_11_out, and_4_out, C);
  and and_12 (and_12_out, and_5_out, C);
  and and_13 (and_13_out, A, B);
  and and_14 (and_14_out, and_6_out, not_5_out);
  and and_15 (and_15_out, and_7_out, D);
  and and_16 (and_16_out, A, not_7_out);
  and and_17 (and_17_out, and_8_out, D);
  and and_18 (and_18_out, and_9_out, D);
  or or_2 (or_2_out, and_11_out, and_12_out);
  and and_19 (and_19_out, and_13_out, D);
  or or_3 (or_3_out, and_14_out, and_15_out);
  and and_20 (and_20_out, and_16_out, D);
  or or_4 (T, and_17_out, and_18_out);
  or or_5 (E, or_2_out, and_19_out);
  or or_6 (R, or_3_out, and_20_out);

  assign I = D;
  assign U = 1'b0;
endmodule

module _9_s_comp_BCD (
  input  A,
  input  B,
  input  C,
  input  D,
  output Q,
  output W,
  output E,
  output R
);

  wire and_2_out, and_3_out, not_1_out, not_2_out, not_3_out, not_4_out, not_5_out;

  not not_1 (not_1_out, A);
  not not_2 (not_2_out, B);
  and and_1 (Q, not_1_out, not_2_out, not_3_out);
  not not_3 (not_3_out, C);
  not not_4 (not_4_out, B);
  and and_2 (and_2_out, not_4_out, C);
  and and_3 (and_3_out, B, not_5_out);
  not not_5 (not_5_out, C);
  not not_6 (R, D);
  or or_1 (W, and_2_out, and_3_out);

  assign E = C;
endmodule

module _10_s_comp (
  input  A,
  input  B,
  input  C,
  input  D,
  output Q,
  output W,
  output E,
  output R
);

  wire and_1_out, and_2_out, and_3_out, and_4_out, and_5_out, and_6_out, and_7_out, and_8_out, and_9_out,
       and_10_out, not_1_out, not_2_out, not_3_out, not_4_out, not_5_out, not_6_out, not_7_out, not_8_out,
       not_9_out, not_10_out, not_11_out;

  not not_1 (not_1_out, A);
  not not_2 (not_2_out, B);
  and and_1 (and_1_out, not_1_out, not_2_out, not_3_out);
  not not_3 (not_3_out, C);
  not not_4 (not_4_out, B);
  and and_2 (and_2_out, not_4_out, C, not_5_out);
  not not_5 (not_5_out, D);
  not not_6 (not_6_out, B);
  and and_3 (and_3_out, not_6_out, C, D);
  and and_4 (and_4_out, B, not_7_out);
  not not_7 (not_7_out, C);
  and and_5 (and_5_out, B, not_8_out);
  not not_8 (not_8_out, D);
  and and_6 (and_6_out, A, C);
  not not_9 (not_9_out, C);
  and and_7 (and_7_out, not_9_out, not_10_out);
  not not_10 (not_10_out, D);
  and and_8 (and_8_out, C, D);
  and and_9 (and_9_out, A, not_11_out);
  not not_11 (not_11_out, D);
  and and_10 (and_10_out, A, C);
  or or_1 (Q, and_1_out, and_2_out);
  or or_2 (W, and_3_out, and_4_out, and_5_out, and_6_out);
  or or_3 (E, and_7_out, and_8_out, and_9_out);
  or or_4 (R, D, and_10_out);
endmodule
