// Logisim project q5 HA FA HS FS.circ as structural Verilog: 1 circuit, main circuit main
module main (
  input  in_1,
  input  A,
  input  in_3,
  input  B,
  input  in_5,
  input  in_6,
  input  in_7,
  input  in_8,
  input  in_9,
  input  in_10,
  output SUM,
  output SUM_2,
  output CARRY,
  output CARRY_2,
  output DIFFERENCE,
  output out_16,
  output BORROW,
  output BORROW_2
);

  wire and_3_out, and_4_out, and_5_out, and_6_out, not_1_out, not_2_out, not_3_out, xor_3_out, xor_4_out;

  not not_1 (not_1_out, in_6);
  xor xor_1 (SUM_2, A, B);
  xor xor_2 (DIFFERENCE, in_6, in_8);
  and and_1 (BORROW, not_1_out, in_8);
  and and_2 (CARRY, B, A);
  and and_3 (and_3_out, in_1, in_3);
  xor xor_3 (xor_3_out, in_1, in_3);
  xor xor_4 (xor_4_out, in_7, in_9);
  not not_2 (not_2_out, in_7);
  and and_4 (and_4_out, not_2_out, in_9);
  xor xor_5 (out_16, xor_4_out, in_10);
  not not_3 (not_3_out, xor_4_out);
  xor xor_6 (SUM, xor_3_out, in_5);
  and and_5 (and_5_out, xor_3_out, in_5);
  or or_1 (CARRY_2, and_3_out, and_5_out);
  and and_6 (and_6_out, not_3_out, in_10);
  or or_2 (BORROW_2, and_6_out, and_4_out);

  // Notes on the sheet:
  //   HALF ADDER
  //   HALF SUBTRACTOR
  //   FULL ADDER
  //   FULL SUBTRACTOR
  //   DIFFFERENCE
endmodule
