// Logisim project q6 a 4bit adder using decoder.circ as structural Verilog: 3 circuits, main circuit Decoder
module Decoder (
  input  in_1,
  input  in_2,
  input  in_3,
  output out_4,
  output out_5,
  output out_6,
  output out_7,
  output out_8,
  output out_9,
  output out_10,
  output out_11
);

  wire not_1_out, not_2_out, not_3_out;

  not not_1 (not_1_out, in_1);
  not not_2 (not_2_out, in_3);
  not not_3 (not_3_out, in_2);
  and and_1 (out_4, not_2_out, not_3_out, not_1_out);
  and and_2 (out_5, in_3, not_3_out, not_1_out);
  and and_3 (out_6, in_2, not_2_out, not_1_out);
  and and_4 (out_7, in_3, in_2, not_1_out);
  and and_5 (out_8, in_1, not_3_out, not_2_out);
  and and_6 (out_9, in_1, in_3, not_3_out);
  and and_7 (out_10, in_1, in_2, not_2_out);
  and and_8 (out_11, in_1, in_2, in_3);
endmodule

module full_adder (
  input  in_1,
  input  in_2,
  input  in_3,
  output out_4,
  output out_5
);

  wire decoder_1_out_5, decoder_1_out_6, decoder_1_out_7, decoder_1_out_8, decoder_1_out_9, decoder_1_out_10,
       decoder_1_out_11;

  Decoder decoder_1 (
    .out_5(decoder_1_out_5), .out_6(decoder_1_out_6), .out_7(decoder_1_out_7), .out_8(decoder_1_out_8),
    .out_9(decoder_1_out_9), .out_10(decoder_1_out_10), .out_11(decoder_1_out_11), .in_1(in_1), .in_2(in_2),
    .in_3(in_3));  // open: out_4
  or or_1 (out_4, decoder_1_out_11, decoder_1_out_8, decoder_1_out_6, decoder_1_out_5);
  or or_2 (out_5, decoder_1_out_11, decoder_1_out_10, decoder_1_out_7, decoder_1_out_9);
endmodule

module _4_bit_adder (
  input  A0,
  input  B0,
  input  A1,
  input  B1,
  input  A2,
  input  B2,
  input  A3,
  input  in_8,
  input  in_9,
  output c0,
  output c1,
  output c2,
  output c3,
  output cout
);

  wire full_adder_1_out_5, full_adder_2_out_5, full_adder_3_out_5;

  full_adder full_adder_1 (.in_1(in_9), .in_2(A0), .in_3(B0), .out_4(c0), .out_5(full_adder_1_out_5));
  full_adder full_adder_2 (.in_1(full_adder_1_out_5), .in_2(A1), .in_3(B1), .out_4(c1), .out_5(full_adder_2_out_5));
  full_adder full_adder_3 (.in_1(full_adder_2_out_5), .in_2(A2), .in_3(B2), .out_4(c2), .out_5(full_adder_3_out_5));
  full_adder full_adder_4 (.in_1(full_adder_3_out_5), .in_2(A3), .in_3(in_8), .out_4(c3), .out_5(cout));

  // Notes on the sheet:
  //   B3
endmodule
