// Logisim project q6 c 4bit subtractor using decoder.circ as structural Verilog: 3 circuits, main circuit Decoder
module Decoder (
  input  in_1,
  input  in_2,
  input  in_3,
  output out_4,
  output out_5,
  output out_6,
  output out_7,
  output out_8,
  output out_9,
  output out_10,
  output out_11
);

  wire not_1_out, not_2_out, not_3_out;

  not not_1 (not_1_out, in_1);
  not not_2 (not_2_out, in_2);
  not not_3 (not_3_out, in_3);
  and and_1 (out_4, not_3_out, not_2_out, not_1_out);
  and and_2 (out_5, in_3, not_2_out, not_1_out);
  and and_3 (out_6, in_2, not_3_out, not_1_out);
  and and_4 (out_7, in_3, in_2, not_1_out);
  and and_5 (out_8, in_1, not_2_out, not_3_out);
  and and_6 (out_9, in_1, in_3, not_2_out);
  and and_7 (out_10, in_1, in_2, not_3_out);
  and and_8 (out_11, in_1, in_2, in_3);
endmodule

module full_adder (
  input  in_1,
  input  in_2,
  input  in_3,
  output out_4,
  output out_5
);

  wire decoder_1_out_5, decoder_1_out_6, decoder_1_out_7, decoder_1_out_8, decoder_1_out_9, decoder_1_out_10,
       decoder_1_out_11;

  Decoder decoder_1 (
    .out_5(decoder_1_out_5), .out_6(decoder_1_out_6), .out_7(decoder_1_out_7), .out_8(decoder_1_out_8),
    .out_9(decoder_1_out_9), .out_10(decoder_1_out_10), .out_11(decoder_1_out_11), .in_1(in_1), .in_2(in_2),
    .in_3(in_3));  // open: out_4
  or or_1 (out_4, decoder_1_out_11, decoder_1_out_8, decoder_1_out_6, decoder_1_out_5);
  or or_2 (out_5, decoder_1_out_11, decoder_1_out_10, decoder_1_out_7, decoder_1_out_9);
endmodule

module _4_bit_adder (
  input  b0,
  input  b1,
  input  b2,
  input  b3,
  input  a0,
  input  a1,
  input  a2,
  input  a3,
  input  in_9,
  output v,
  output cout,
  output c3,
  output c2,
  output c1,
  output c0
);

  wire full_adder_1_out_5, full_adder_2_out_5, full_adder_3_out_5, xor_1_out, xor_2_out, xor_3_out, xor_4_out;

  xor xor_1 (xor_1_out, in_9, b0);
  full_adder full_adder_1 (.in_1(in_9), .in_2(a0), .in_3(xor_1_out), .out_4(c0), .out_5(full_adder_1_out_5));
  full_adder full_adder_2 (
    .in_1(full_adder_1_out_5), .in_2(a1), .in_3(xor_2_out), .out_4(c1), .out_5(full_adder_2_out_5));
  xor xor_2 (xor_2_out, in_9, b1);
  xor xor_3 (xor_3_out, in_9, b2);
  full_adder full_adder_3 (
    .in_1(full_adder_2_out_5), .in_2(a2), .in_3(xor_3_out), .out_4(c2), .out_5(full_adder_3_out_5));
  full_adder full_adder_4 (.in_1(full_adder_3_out_5), .in_2(a3), .in_3(xor_4_out), .out_4(c3), .out_5(cout));
  xor xor_4 (xor_4_out, in_9, b3);
  xor xor_5 (v, cout, full_adder_3_out_5);

  // Notes on the sheet:
  //   A0
  //   B0
  //   A1
  //   B1
  //   B2
  //   A2
  //   A3
  //   B3
endmodule
