// Logisim project q6 d 4 bit subtractor using mux.circ as structural Verilog: 3 circuits, main circuit mux
module mux (
  input  in_1,
  input  in_2,
  input  in_3,
  input  in_4,
  input  in_5,
  input  in_6,
  output out_7
);

  wire and_1_out, and_2_out, and_3_out, and_4_out, not_1_out, not_2_out;

  not not_1 (not_1_out, in_1);
  not not_2 (not_2_out, in_2);
  and and_1 (and_1_out, not_2_out, in_3, not_1_out);
  and and_2 (and_2_out, not_1_out, not_1_out, in_4, in_2);
  and and_3 (and_3_out, in_1, in_5, not_2_out);
  and and_4 (and_4_out, in_2, in_1, in_6);
  or or_1 (out_7, and_1_out, and_2_out, and_3_out, and_4_out);
endmodule

module full_adder (
  input  in_1,
  input  in_2,
  input  in_3,
  output out_4,
  output out_5
);

  wire not_1_out;

  not not_1 (not_1_out, in_1);
  mux mux_1 (.in_1(in_2), .in_2(in_3), .in_3(1'b0), .in_4(in_1), .in_5(in_1), .in_6(1'b1), .out_7(out_5));
  mux mux_2 (.in_1(in_2), .in_2(in_3), .in_3(in_1), .in_4(not_1_out), .in_5(not_1_out), .in_6(in_1), .out_7(out_4));
endmodule

module _4_bit_adder (
  input  a0,
  input  a1,
  input  a2,
  input  a3,
  input  b0,
  input  b1,
  input  b2,
  input  b3,
  input  in_9,
  output v,
  output cout,
  output c3,
  output c2,
  output c1,
  output c0
);

  wire full_adder_1_out_5, full_adder_2_out_5, full_adder_3_out_5, xor_1_out, xor_2_out, xor_3_out, xor_4_out;

  xor xor_1 (xor_1_out, a0, in_9);
  full_adder full_adder_1 (.out_5(full_adder_1_out_5), .in_1(in_9), .in_2(b0), .in_3(xor_1_out), .out_4(c0));
  xor xor_2 (xor_2_out, in_9, a1);
  full_adder full_adder_2 (
    .out_5(full_adder_2_out_5), .in_1(full_adder_1_out_5), .in_2(b1), .in_3(xor_2_out), .out_4(c1));
  full_adder full_adder_3 (
    .out_5(full_adder_3_out_5), .in_1(full_adder_2_out_5), .in_2(b2), .in_3(xor_3_out), .out_4(c2));
  xor xor_3 (xor_3_out, in_9, a2);
  full_adder full_adder_4 (.out_5(cout), .in_1(full_adder_3_out_5), .in_2(b3), .in_3(xor_4_out), .out_4(c3));
  xor xor_4 (xor_4_out, in_9, a3);
  xor xor_5 (v, full_adder_3_out_5, cout);
endmodule
