// Logisim project submission.circ as structural Verilog: 8 circuits, main circuit q1
module q1 (
  input  A,
  input  A_2,
  input  B,
  input  B_2,
  input  A_3,
  input  A_4,
  input  A_5,
  input  B_3,
  input  B_4,
  input  A_6,
  input  A_7,
  input  B_5,
  input  B_6,
  output O,
  output O_2,
  output O_3,
  output O_4,
  output O_5,
  output O_6,
  output O_7
);

  and and_1 (O, A, B);
  not not_1 (O_3, A_3);
  nand nand_1 (O_4, A_4, B_3);
  xor xor_1 (O_6, A_6, B_5);
  or or_1 (O_2, A_2, B_2);
  nor nor_1 (O_5, A_5, B_4);
  xnor xnor_1 (O_7, A_7, B_6);

  // Notes on the sheet:
  //   AND Gate
  //   NOT Gate
  //   NAND Gate
  //   XOR Gate
  //   OR Gate
  //   NOR Gate
  //   XNOR Gate
endmodule

module q2 (
  input  A,
  input  A_2,
  input  A_3,
  input  A_4,
  input  B,
  input  B_2,
  input  B_3,
  input  B_4,
  input  A_5,
  input  A_6,
  input  A_7,
  input  B_5,
  input  A_8,
  input  A_9,
  input  A_10,
  input  B_6,
  input  B_7,
  input  B_8,
  input  A_11,
  input  A_12,
  input  B_9,
  input  B_10,
  output O,
  output O_2,
  output O_3,
  output O_4,
  output O_5,
  output O_6,
  output O_7,
  output O_8,
  output O_9,
  output O_10,
  output O_11,
  output O_12
);

  wire nand_1_out, nand_3_out, nand_4_out, nand_5_out, nand_6_out, nand_8_out, nand_9_out, nand_10_out,
       nand_13_out, nand_14_out, nand_16_out, nand_17_out, nand_18_out, nand_19_out, nor_1_out, nor_2_out,
       nor_4_out, nor_5_out, nor_6_out, nor_7_out, nor_9_out, nor_10_out, nor_11_out, nor_14_out, nor_15_out,
       nor_16_out, nor_17_out, nor_18_out;

  nand nand_1 (nand_1_out, A_2, B_2);
  nand nand_2 (O_5, A_5, A_5);
  nand nand_3 (nand_3_out, A_7, A_7);
  nand nand_4 (nand_4_out, B_5, B_5);
  nand nand_5 (nand_5_out, B_8, B_8);
  nand nand_6 (nand_6_out, A_10, A_10);
  nand nand_7 (O, nand_1_out, nand_1_out);
  nand nand_8 (nand_8_out, nand_3_out, nand_4_out);
  nand nand_9 (nand_9_out, A_10, nand_5_out);
  nand nand_10 (nand_10_out, B_8, nand_6_out);
  nand nand_11 (O_7, nand_8_out, nand_8_out);
  nand nand_12 (O_9, nand_9_out, nand_10_out);
  nand nand_13 (nand_13_out, A, A);
  nand nand_14 (nand_14_out, B, B);
  nand nand_15 (O_3, nand_13_out, nand_14_out);
  nand nand_16 (nand_16_out, A_9, A_9);
  nand nand_17 (nand_17_out, B_7, B_7);
  nand nand_18 (nand_18_out, nand_16_out, nand_17_out);
  nand nand_19 (nand_19_out, A_9, B_7);
  nand nand_20 (O_10, nand_18_out, nand_19_out);
  nor nor_1 (nor_1_out, A_3, A_3);
  nor nor_2 (nor_2_out, B_3, B_3);
  nor nor_3 (O_6, A_6, A_6);
  nor nor_4 (nor_4_out, A_8, A_8);
  nor nor_5 (nor_5_out, B_6, B_6);
  nor nor_6 (nor_6_out, A_12, A_12);
  nor nor_7 (nor_7_out, B_10, B_10);
  nor nor_8 (O_4, nor_1_out, nor_2_out);
  nor nor_9 (nor_9_out, nor_4_out, nor_5_out);
  nor nor_10 (nor_10_out, nor_6_out, nor_7_out);
  nor nor_11 (nor_11_out, A_12, B_10);
  nor nor_12 (O_8, nor_9_out, nor_9_out);
  nor nor_13 (O_12, nor_10_out, nor_11_out);
  nor nor_14 (nor_14_out, B_9, B_9);
  nor nor_15 (nor_15_out, A_11, A_11);
  nor nor_16 (nor_16_out, A_4, B_4);
  nor nor_17 (nor_17_out, A_11, nor_14_out);
  nor nor_18 (nor_18_out, B_9, nor_15_out);
  nor nor_19 (O_2, nor_16_out, nor_16_out);
  nor nor_20 (O_11, nor_17_out, nor_18_out);

  // Notes on the sheet:
  //   Using NAND Gates
  //   AND Gate
  //   NOT Gate
  //   NOR Gate
  //   XOR Gate
  //   OR Gate
  //   XNOR Gate
  //   AND Gate
  //   NOT Gate
  //   XOR Gate
  //   Using NOR Gates
  //   NAND Gate
  //   OR Gate
  //   XNOR Gate
endmodule

module q3_NAND (
  input  A,
  input  B,
  input  C,
  input  D,
  input  A_2,
  input  B_2,
  input  C_2,
  input  D_2,
  output W,
  output X,
  output Y,
  output Z,
  output W_2,
  output X_2,
  output Y_2,
  output Z_2
);

  wire nand_1_out, nand_2_out, nand_3_out, nand_4_out, nand_5_out, nand_6_out, nand_7_out, nand_8_out,
       nand_9_out, nand_10_out, nand_11_out, nand_12_out, nand_13_out, nand_14_out, nand_15_out, nand_16_out,
       nand_17_out, nand_18_out, nand_19_out, nand_21_out, nand_22_out, nand_23_out, nand_24_out,
       nand_25_out, nand_26_out, nand_27_out, nand_28_out, nand_29_out, nand_30_out, nand_31_out, nand_32_out;

  nand nand_1 (nand_1_out, A_2, A_2);
  nand nand_2 (nand_2_out, B_2, B_2);
  nand nand_3 (nand_3_out, C_2, C_2);
  nand nand_4 (nand_4_out, A_2, A_2);
  nand nand_5 (nand_5_out, B_2, B_2);
  nand nand_6 (nand_6_out, D_2, D_2);
  nand nand_7 (nand_7_out, B_2, B_2);
  nand nand_8 (nand_8_out, C_2, C_2);
  nand nand_9 (nand_9_out, D_2, D_2);
  nand nand_10 (nand_10_out, C_2, C_2);
  nand nand_11 (nand_11_out, D_2, D_2);
  nand nand_12 (nand_12_out, A_2, A_2);
  nand nand_13 (nand_13_out, B_2, B_2);
  nand nand_14 (nand_14_out, C_2, C_2);
  nand nand_15 (nand_15_out, A, A);
  nand nand_16 (nand_16_out, B, B);
  nand nand_17 (nand_17_out, C, C);
  nand nand_18 (nand_18_out, B, B);
  nand nand_19 (nand_19_out, C, C);
  nand nand_20 (Z, D, D);
  nand nand_21 (nand_21_out, nand_1_out, nand_2_out, nand_3_out);
  nand nand_22 (nand_22_out, nand_4_out, nand_5_out, nand_6_out);
  nand nand_23 (nand_23_out, nand_7_out, C_2, D_2);
  nand nand_24 (nand_24_out, B_2, nand_8_out);
  nand nand_25 (nand_25_out, B_2, nand_9_out);
  nand nand_26 (nand_26_out, nand_10_out, nand_11_out);
  nand nand_27 (nand_27_out, C_2, D_2);
  nand nand_28 (nand_28_out, nand_12_out, nand_13_out, nand_14_out);
  nand nand_29 (nand_29_out, D_2, D_2);
  nand nand_30 (nand_30_out, nand_15_out, nand_16_out, nand_17_out);
  nand nand_31 (nand_31_out, nand_18_out, C);
  nand nand_32 (nand_32_out, B, nand_19_out);
  nand nand_33 (W_2, nand_21_out, nand_22_out);
  nand nand_34 (X_2, nand_23_out, nand_24_out, nand_25_out);
  nand nand_35 (Y_2, nand_26_out, nand_27_out);
  nand nand_36 (Z_2, nand_28_out, nand_29_out);
  nand nand_37 (W, nand_30_out, nand_30_out);
  nand nand_38 (X, nand_31_out, nand_32_out);

  assign Y = C;

  // Notes on the sheet:
  //   9's complement
  //   10's complement
endmodule

module q3_NOR (
  input  A,
  input  B,
  input  C,
  input  D,
  input  A_2,
  input  B_2,
  input  C_2,
  input  D_2,
  output Q,
  output W,
  output E,
  output R,
  output Q_2,
  output W_2,
  output E_2,
  output R_2
);

  wire nor_3_out, nor_4_out, nor_5_out, nor_6_out, nor_7_out, nor_8_out, nor_9_out, nor_10_out, nor_11_out,
       nor_12_out, nor_13_out, nor_14_out, nor_16_out, nor_17_out, nor_18_out, nor_19_out, nor_20_out,
       nor_21_out, nor_22_out, nor_23_out, nor_24_out, nor_25_out, nor_26_out, nor_27_out, nor_28_out,
       nor_29_out, nor_30_out, nor_31_out, nor_32_out, nor_33_out, nor_34_out, nor_36_out, nor_39_out;

  nor nor_1 (Q, A, B, C);
  nor nor_2 (R, D, D);
  nor nor_3 (nor_3_out, B, B);
  nor nor_4 (nor_4_out, C, C);
  nor nor_5 (nor_5_out, nor_3_out, nor_4_out);
  nor nor_6 (nor_6_out, B, C);
  nor nor_7 (nor_7_out, C_2, C_2);
  nor nor_8 (nor_8_out, C_2, C_2);
  nor nor_9 (nor_9_out, D_2, D_2);
  nor nor_10 (nor_10_out, B_2, B_2);
  nor nor_11 (nor_11_out, B_2, B_2);
  nor nor_12 (nor_12_out, A_2, A_2);
  nor nor_13 (nor_13_out, C_2, C_2);
  nor nor_14 (nor_14_out, D_2, D_2);
  nor nor_15 (W, nor_5_out, nor_6_out);
  nor nor_16 (nor_16_out, A_2, B_2, C_2);
  nor nor_17 (nor_17_out, B_2, nor_8_out, nor_9_out);
  nor nor_18 (nor_18_out, nor_10_out, C_2);
  nor nor_19 (nor_19_out, nor_11_out, D_2);
  nor nor_20 (nor_20_out, nor_12_out, nor_13_out);
  nor nor_21 (nor_21_out, D_2, D_2);
  nor nor_22 (nor_22_out, C_2, C_2);
  nor nor_23 (nor_23_out, nor_14_out, nor_14_out);
  nor nor_24 (nor_24_out, A_2, A_2);
  nor nor_25 (nor_25_out, nor_7_out, B_2, D_2);
  nor nor_26 (nor_26_out, C_2, nor_21_out);
  nor nor_27 (nor_27_out, D_2, nor_22_out);
  nor nor_28 (nor_28_out, nor_23_out, nor_24_out);
  nor nor_29 (nor_29_out, C_2, C_2);
  nor nor_30 (nor_30_out, A_2, A_2);
  nor nor_31 (nor_31_out, nor_16_out, nor_25_out);
  nor nor_32 (nor_32_out, nor_17_out, nor_18_out, nor_19_out, nor_20_out);
  nor nor_33 (nor_33_out, nor_26_out, nor_27_out);
  nor nor_34 (nor_34_out, nor_33_out, nor_28_out);
  nor nor_35 (Q_2, nor_31_out, nor_31_out);
  nor nor_36 (nor_36_out, nor_29_out, nor_30_out);
  nor nor_37 (W_2, nor_32_out, nor_32_out);
  nor nor_38 (E_2, nor_34_out, nor_34_out);
  nor nor_39 (nor_39_out, nor_36_out, D_2);
  nor nor_40 (R_2, nor_39_out, nor_39_out);

  assign E = C;

  // Notes on the sheet:
  //   9's Complement
  //   10's Complement
endmodule

module q4_a (
  input  A,
  input  B,
  input  C,
  input  D,
  input  A_2,
  input  B_2,
  input  C_2,
  input  D_2,
  output W,
  output X,
  output Y,
  output Z,
  output W_2,
  output X_2,
  output Y_2,
  output Z_2
);

  wire and_1_out, and_2_out, and_3_out, and_4_out, and_5_out, and_6_out, and_7_out, and_8_out, and_9_out,
       and_10_out, and_11_out, and_12_out, and_13_out, and_14_out, and_15_out, and_16_out, and_17_out,
       and_18_out, and_19_out, and_20_out, not_1_out, not_2_out, not_3_out, not_4_out, not_5_out, not_6_out,
       not_7_out, not_8_out, not_9_out, not_10_out, not_11_out, not_12_out, not_13_out, not_14_out,
       not_15_out, not_16_out, not_17_out, not_18_out, not_19_out, not_20_out, not_21_out, not_22_out,
       not_23_out, not_24_out, not_25_out, not_26_out, not_27_out, not_28_out, not_29_out, not_30_out;

  not not_1 (not_1_out, A);
  not not_2 (not_2_out, B);
  not not_3 (not_3_out, B);
  not not_4 (not_4_out, C);
  not not_5 (not_5_out, C);
  not not_6 (not_6_out, D);
  not not_7 (not_7_out, A_2);
  not not_8 (not_8_out, B_2);
  not not_9 (not_9_out, A_2);
  not not_10 (not_10_out, B_2);
  not not_11 (not_11_out, A_2);
  not not_12 (not_12_out, C_2);
  not not_13 (not_13_out, B_2);
  not not_14 (not_14_out, C_2);
  not not_15 (not_15_out, A_2);
  not not_16 (not_16_out, B_2);
  not not_17 (not_17_out, C_2);
  not not_18 (not_18_out, A_2);
  not not_19 (not_19_out, B_2);
  not not_20 (not_20_out, D_2);
  not not_21 (not_21_out, A_2);
  not not_22 (not_22_out, C_2);
  not not_23 (not_23_out, D_2);
  not not_24 (not_24_out, A_2);
  not not_25 (not_25_out, B_2);
  not not_26 (not_26_out, C_2);
  not not_27 (not_27_out, D_2);
  not not_28 (not_28_out, B_2);
  not not_29 (not_29_out, C_2);
  not not_30 (not_30_out, D_2);
  and and_1 (and_1_out, not_1_out, B);
  and and_2 (and_2_out, A, not_2_out);
  and and_3 (and_3_out, not_3_out, C);
  and and_4 (and_4_out, B, not_4_out);
  and and_5 (and_5_out, not_5_out, D);
  and and_6 (and_6_out, C, not_6_out);
  and and_7 (and_7_out, not_7_out, B_2);
  and and_8 (and_8_out, A_2, not_8_out);
  and and_9 (and_9_out, not_9_out, not_10_out, C_2);
  and and_10 (and_10_out, not_11_out, B_2, not_12_out);
  and and_11 (and_11_out, A_2, not_13_out, not_14_out);
  and and_12 (and_12_out, A_2, B_2, C_2);
  and and_13 (and_13_out, not_15_out, not_16_out, not_17_out, D_2);
  and and_14 (and_14_out, not_18_out, not_19_out, C_2, not_20_out);
  and and_15 (and_15_out, not_21_out, B_2, not_22_out, not_23_out);
  and and_16 (and_16_out, not_24_out, B_2, C_2, D_2);
  and and_17 (and_17_out, A_2, not_25_out, not_26_out, not_27_out);
  and and_18 (and_18_out, A_2, not_28_out, C_2, D_2);
  and and_19 (and_19_out, A_2, B_2, not_29_out, D_2);
  and and_20 (and_20_out, A_2, B_2, C_2, not_30_out);
  or or_1 (X, and_1_out, and_2_out);
  or or_2 (Y, and_3_out, and_4_out);
  or or_3 (Z, and_5_out, and_6_out);
  or or_4 (X_2, and_7_out, and_8_out);
  or or_5 (Y_2, and_9_out, and_10_out, and_11_out, and_12_out);
  or or_6 (Z_2, and_13_out, and_14_out, and_15_out, and_16_out, and_17_out, and_18_out, and_19_out, and_20_out);

  assign W = A;
  assign W_2 = A_2;

  // Notes on the sheet:
  //   Binary to gray code
  //   Gray Code to Binary
endmodule

module q4_b (
  input  A,
  input  B,
  input  C,
  input  D,
  input  A_2,
  input  B_2,
  input  C_2,
  input  D_2,
  output W,
  output X,
  output Y,
  output Z,
  output W_2,
  output X_2,
  output Y_2,
  output Z_2
);

  wire and_1_out, and_2_out, and_3_out, and_4_out, and_5_out, and_6_out, and_7_out, and_8_out, and_9_out,
       and_10_out, and_11_out, and_12_out, and_13_out, and_14_out, not_1_out, not_2_out, not_3_out,
       not_4_out, not_5_out, not_6_out, not_8_out, not_9_out, not_10_out, not_11_out, not_12_out, not_13_out;

  and and_1 (and_1_out, B, D);
  and and_2 (and_2_out, B, C);
  not not_1 (not_1_out, B);
  not not_2 (not_2_out, B);
  not not_3 (not_3_out, C);
  not not_4 (not_4_out, D);
  not not_5 (not_5_out, C);
  not not_6 (not_6_out, D);
  not not_7 (Z, D);
  and and_3 (and_3_out, A_2, C_2, D_2);
  and and_4 (and_4_out, A_2, B_2);
  not not_8 (not_8_out, B_2);
  not not_9 (not_9_out, C_2);
  not not_10 (not_10_out, B_2);
  not not_11 (not_11_out, D_2);
  not not_12 (not_12_out, C_2);
  not not_13 (not_13_out, D_2);
  not not_14 (Z_2, D_2);
  or or_1 (W, and_1_out, and_2_out, A);
  and and_5 (and_5_out, not_1_out, D);
  and and_6 (and_6_out, not_2_out, C);
  and and_7 (and_7_out, B, not_3_out, not_4_out);
  and and_8 (and_8_out, not_5_out, not_6_out);
  and and_9 (and_9_out, C, D);
  or or_2 (W_2, and_3_out, and_4_out);
  and and_10 (and_10_out, not_8_out, not_9_out);
  and and_11 (and_11_out, not_10_out, not_11_out);
  and and_12 (and_12_out, B_2, C_2, D_2);
  and and_13 (and_13_out, not_12_out, D_2);
  and and_14 (and_14_out, C_2, not_13_out);
  or or_3 (X, and_5_out, and_6_out, and_7_out);
  or or_4 (Y, and_8_out, and_9_out);
  or or_5 (X_2, and_10_out, and_11_out, and_12_out);
  or or_6 (Y_2, and_13_out, and_14_out);

  // Notes on the sheet:
  //   BCD to Excess 3
  //   Excess 3 to BCD
endmodule

module q4_c (
  input  A,
  input  B,
  input  C,
  input  D,
  output Q,
  output W,
  output E,
  output R,
  output T,
  output Y,
  output U,
  output I
);

  wire and_2_out, and_3_out, and_4_out, and_5_out, and_6_out, and_7_out, and_8_out, and_9_out, and_10_out,
       and_11_out, and_12_out, and_13_out, and_14_out, and_15_out, and_16_out, and_17_out, and_19_out,
       and_20_out, not_1_out, not_2_out, not_3_out, not_4_out, not_5_out, not_6_out, not_7_out, not_8_out,
       not_9_out, not_10_out, or_2_out, or_3_out;

  and and_1 (Q, A, B);
  not not_1 (not_1_out, B);
  not not_2 (not_2_out, A);
  not not_3 (not_3_out, B);
  not not_4 (not_4_out, C);
  not not_5 (not_5_out, A);
  not not_6 (not_6_out, B);
  not not_7 (not_7_out, C);
  not not_8 (not_8_out, D);
  and and_2 (and_2_out, A, not_1_out);
  or or_1 (W, and_2_out, and_3_out);
  and and_3 (and_3_out, A, C);
  and and_4 (and_4_out, not_2_out, B);
  and and_5 (and_5_out, and_4_out, C);
  and and_6 (and_6_out, A, not_3_out);
  and and_7 (and_7_out, and_6_out, C);
  and and_8 (and_8_out, A, B);
  and and_9 (and_9_out, B, not_4_out);
  and and_10 (and_10_out, and_9_out, not_9_out);
  not not_9 (not_9_out, D);
  and and_11 (and_11_out, not_5_out, B);
  and and_12 (and_12_out, and_11_out, D);
  and and_13 (and_13_out, A, not_10_out);
  not not_10 (not_10_out, B);
  and and_14 (and_14_out, not_6_out, C);
  and and_15 (and_15_out, and_14_out, D);
  and and_16 (and_16_out, B, not_7_out);
  and and_17 (and_17_out, and_16_out, D);
  and and_18 (Y, C, not_8_out);
  or or_2 (or_2_out, and_5_out, and_7_out);
  and and_19 (and_19_out, and_8_out, D);
  or or_3 (or_3_out, and_10_out, and_12_out);
  and and_20 (and_20_out, and_13_out, D);
  or or_4 (T, and_15_out, and_17_out);
  or or_5 (E, or_2_out, and_19_out);
  or or_6 (R, or_3_out, and_20_out);

  assign I = D;
  assign U = 1'b0;

  // Notes on the sheet:
  //   Binary Number equal to square of input
endmodule

module q4_d (
  input  A,
  input  B,
  input  C,
  input  D,
  output Q,
  output W,
  output E,
  output R
);

  wire and_2_out, and_3_out, not_1_out, not_2_out, not_3_out, not_4_out, not_5_out;

  not not_1 (not_1_out, A);
  not not_2 (not_2_out, B);
  not not_3 (not_3_out, C);
  not not_4 (not_4_out, B);
  not not_5 (not_5_out, C);
  not not_6 (R, D);
  and and_1 (Q, not_1_out, not_2_out, not_3_out);
  and and_2 (and_2_out, not_4_out, C);
  and and_3 (and_3_out, B, not_5_out);
  or or_1 (W, and_2_out, and_3_out);

  assign E = C;

  // Notes on the sheet:
  //   9's Complement of decimal BCD
endmodule
